// Digital circuit cpu.dig as structural Verilog
module cpu (
  input  CLK,
  input  HLT,
  output [31:0] RS1,
  output [31:0] RS2,
  output [31:0] RegBus,
  output [1:0] out_5,
  output [31:0] ImmBus,
  output [31:0] MemoryAddressBus,
  output [11:0] out_9,
  output [31:0] MemoryOUTBus,
  output out_11,
  output NOT_EN
);

  wire add_1_c_o, and_1_out, and_2_out, and_3_out, comparator_1_eq, comparator_2_eq, comparator_3_eq,
       comparator_5_eq, d_ff_3_q, decoder_1_out_1, decoder_1_out_2, decoder_1_out_3, decoder_1_out_4,
       decoder_1_out_5, decoder_1_out_6, decoder_1_out_7, decoder_1_out_8, decoder_1_out_9, decoder_1_out_10,
       decoder_1_out_11, decoder_1_out_12, decoder_1_out_13, decoder_1_out_14, decoder_1_out_15,
       decoder_2_out_0, decoder_2_out_1, decoder_2_out_2, decoder_2_out_3, decoder_2_out_4, decoder_2_out_5,
       decoder_2_out_6, decoder_2_out_7, decoder_2_out_8, decoder_2_out_9, decoder_2_out_10,
       decoder_2_out_11, decoder_2_out_12, decoder_2_out_13, decoder_2_out_14, decoder_2_out_15,
       decoder_3_out_0, decoder_3_out_1, decoder_3_out_2, decoder_3_out_3, decoder_3_out_4, decoder_3_out_5,
       decoder_3_out_6, decoder_3_out_7, decoder_3_out_8, decoder_3_out_9, decoder_3_out_10,
       decoder_3_out_11, decoder_3_out_12, decoder_3_out_13, decoder_3_out_14, decoder_3_out_15,
       decoder_4_out_1, decoder_4_out_2, decoder_4_out_3, demultiplexer_7_out_0, demultiplexer_7_out_1,
       demultiplexer_11_out_0, demultiplexer_11_out_1, IRSwitcher_out, not_1_out, not_2_out, not_3_out,
       not_4_out, or_1_out, or_2_out, or_3_out, or_6_out, pulldown_1_out, pulldown_30_out, pulldown_31_out,
       pulldown_41_out, pulldown_42_out, pullup_1_out, pullup_2_out, pullup_3_out;
  wire [0:0] not_5_out, not_6_out, not_7_out, or_9_out, pulldown_10_out, sub_2_c_o;
  wire [1:0] add_1_s, or_8_out, or_8_out_2, or_8_out_3, or_8_out_4, or_10_out, pulldown_5_out,
       pulldown_34_out, pulldown_47_out, pulldown_52_out, rom_1_d_2;
  wire [2:0] demultiplexer_8_out_0, multiplexer_15_out_4;
  wire [3:0] demultiplexer_9_out_0, multiplexer_15_out;
  wire [4:0] demultiplexer_4_out_0, demultiplexer_5_out_1, demultiplexer_6_out_0, demultiplexer_9_out_1,
       multiplexer_15_out_3, multiplexer_15_out_5, multiplexer_15_out_6;
  wire [5:5] comparator_6_eq;
  wire [6:0] demultiplexer_1_out_0, demultiplexer_2_out_1, demultiplexer_3_out_0, multiplexer_18_out,
       or_5_out, pulldown_17_out;
  wire [7:0] demultiplexer_8_out_1, multiplexer_7_out, multiplexer_7_out_2;
  wire [9:0] demultiplexer_4_out_1;
  wire [11:0] demultiplexer_5_out_0;
  wire [12:0] multiplexer_16_out, pulldown_9_out;
  wire [15:0] ramdualport_1_d, ramdualport_1_d_2;
  wire [30:0] pulldown_48_out, pulldown_49_out, pulldown_50_out, pulldown_51_out, pulldown_53_out,
       pulldown_54_out;
  wire [31:0] add_2_s, add_3_s, and_4_out, barrelshifter_1_out, barrelshifter_2_out, barrelshifter_3_out,
       bitextender_1_out, bitextender_2_out, bitextender_3_out, bitextender_4_out, bitextender_5_out,
       bitextender_6_out, counterpreset_1_out, d_ff_1_q, d_ff_2_q, d_ff_4_q, d_ff_5_q, d_ff_6_q, d_ff_7_q,
       d_ff_8_q, d_ff_9_q, d_ff_10_q, d_ff_11_q, d_ff_12_q, d_ff_13_q, d_ff_14_q, d_ff_15_q, d_ff_16_q,
       d_ff_17_q, d_ff_18_q, demultiplexer_10_out_0, demultiplexer_10_out_1, multiplexer_1_out,
       multiplexer_2_out, multiplexer_3_out, multiplexer_4_out, multiplexer_5_out, multiplexer_10_out,
       multiplexer_11_out, multiplexer_12_out, multiplexer_13_out, multiplexer_14_out, multiplexer_17_out,
       multiplexer_19_out, multiplexer_20_out, multiplexer_21_out, multiplexer_22_out, multiplexer_23_out,
       multiplexer_24_out, multiplexer_25_out, multiplexer_26_out, multiplexer_27_out, multiplexer_28_out,
       multiplexer_29_out, multiplexer_30_out, multiplexer_31_out, multiplexer_32_out, multiplexer_33_out,
       multiplexer_34_out, multiplexer_35_out, multiplexer_36_out, multiplexer_37_out, multiplexer_38_out,
       multiplexer_39_out, multiplexer_40_out, or_4_out, or_7_out, pulldown_2_out, pulldown_3_out,
       pulldown_7_out, pulldown_8_out, pulldown_37_out, pulldown_40_out, pulldown_46_out, rom_1_d, sub_1_s,
       sub_2_s, xor_1_out;
  wire [31:6] multiplexer_15_out_2;
  wire [31:24] multiplexer_9_out;

  Multiplexer #(.Selector_Bits(2), .Bits(32)) multiplexer_1 (
    .sel(add_1_s), .in_0({RegBus[7:0], multiplexer_9_out, multiplexer_7_out, multiplexer_7_out_2}),
    .in_1({multiplexer_9_out, RegBus[7:0], multiplexer_7_out, multiplexer_7_out_2}),
    .in_2({multiplexer_7_out, multiplexer_7_out_2, RegBus[7:0], multiplexer_9_out}),
    .in_3({multiplexer_7_out, multiplexer_7_out_2, multiplexer_9_out, RegBus[7:0]}), .out(multiplexer_1_out));
  Multiplexer #(.Bits(32)) multiplexer_2 (
    .sel(add_1_s[1]), .in_0({RegBus[7:0], RegBus[15:8], multiplexer_7_out, multiplexer_7_out_2}),
    .in_1({multiplexer_7_out, multiplexer_7_out_2, RegBus[7:0], RegBus[15:8]}), .out(multiplexer_2_out));
  or or_1 (or_1_out, comparator_5_eq, comparator_1_eq);
  Multiplexer #(.Bits(32)) multiplexer_3 (
    .sel(rom_1_d[25]), .in_0(multiplexer_1_out), .in_1(multiplexer_2_out), .out(multiplexer_3_out));
  Multiplexer #(.Bits(32)) multiplexer_4 (
    .sel(rom_1_d[26]), .in_0({RegBus[7:0], RegBus[15:8], RegBus[23:16], RegBus[31:24]}),
    .in_1(multiplexer_3_out), .out(multiplexer_4_out));
  PullUp pullup_1 (.out(pullup_1_out));
  PullDown pulldown_1 (.out(pulldown_1_out));
  Comparator #(.Bits(4)) comparator_1 (.a(multiplexer_15_out), .b(4'b1100), .eq(comparator_1_eq));  // open: gt, lt
  Demultiplexer #(.Bits(7)) demultiplexer_1 (
    .sel(or_2_out), .in(multiplexer_15_out_2[31:25]), .out_0(demultiplexer_1_out_0),
    .out_1({pulldown_2_out[31], demultiplexer_4_out_1[9:4]}));
  Demultiplexer #(.Bits(7)) demultiplexer_2 (
    .sel(or_1_out), .in(demultiplexer_1_out_0), .out_0(demultiplexer_5_out_0[11:5]),
    .out_1(demultiplexer_2_out_1));
  Demultiplexer #(.Bits(7)) demultiplexer_3 (
    .sel(comparator_5_eq), .in(demultiplexer_2_out_1), .out_0(demultiplexer_3_out_0),
    .out_1({pulldown_9_out[12], pulldown_9_out[10:5]}));
  RAMDualPort #(.AddrBits(20), .isProgramMemory("true"), .Bits(32)) ramdualport_1 (
    .A(MemoryAddressBus[19:0]), .Din(multiplexer_4_out), .str(rom_1_d[20]), .C(CLK), .ld(1'b1),
    .D({ramdualport_1_d_2[7:0], ramdualport_1_d_2[15:8], ramdualport_1_d[7:0], ramdualport_1_d[15:8]}));
  Counter IRSwitcher (.en(pullup_1_out), .C(not_1_out), .clr(pulldown_1_out), .out(IRSwitcher_out));  // open: ovf
  Demultiplexer #(.Bits(5)) demultiplexer_4 (
    .sel(or_2_out), .in(multiplexer_15_out_6), .out_0(demultiplexer_4_out_0),
    .out_1({demultiplexer_4_out_1[3:0], pulldown_2_out[20]}));
  Demultiplexer #(.Bits(5)) demultiplexer_5 (
    .sel(or_1_out), .in(demultiplexer_4_out_0), .out_0(demultiplexer_5_out_0[4:0]),
    .out_1(demultiplexer_5_out_1));
  PullUp pullup_2 (.out(pullup_2_out));
  Demultiplexer #(.Bits(5)) demultiplexer_6 (
    .sel(or_2_out), .in(multiplexer_15_out_5), .out_0(demultiplexer_6_out_0),
    .out_1(demultiplexer_8_out_1[7:3]));
  Multiplexer #(.Bits(32)) multiplexer_5 (
    .sel(demultiplexer_7_out_0), .in_0(d_ff_1_q), .in_1(multiplexer_14_out), .out(multiplexer_5_out));
  Demultiplexer demultiplexer_7 (
    .sel(IRSwitcher_out), .in(pullup_2_out), .out_0(demultiplexer_7_out_0), .out_1(demultiplexer_7_out_1));
  Demultiplexer #(.Bits(3)) demultiplexer_8 (
    .sel(or_2_out), .in(multiplexer_15_out_4), .out_0(demultiplexer_8_out_0),
    .out_1(demultiplexer_8_out_1[2:0]));
  D_FF #(.Bits(32)) d_ff_1 (.D(multiplexer_5_out), .C(not_1_out), .Q(d_ff_1_q));  // open: nQ
  or or_2 (or_2_out, rom_1_d_2[1], or_3_out);
  Multiplexer #(.Bits(16)) multiplexer_6 (
    .sel(add_1_s[1]), .in_0(ramdualport_1_d_2), .in_1(ramdualport_1_d), .out(pulldown_7_out[15:0]));
  Multiplexer #(.Bits(16)) multiplexer_7 (
    .sel(add_1_s[1]), .in_0(ramdualport_1_d), .in_1(ramdualport_1_d_2),
    .out({multiplexer_7_out_2, multiplexer_7_out}));
  or or_3 (or_3_out, comparator_3_eq, comparator_2_eq);
  BitExtender #(.inputBits(20), .outputBits(32)) bitextender_1 (
    .in({pulldown_2_out[31], demultiplexer_4_out_1, pulldown_2_out[20], demultiplexer_8_out_1}),
    .out(bitextender_1_out));
  PullDown #(.Bits(12)) pulldown_2 (.out(pulldown_2_out[11:0]));
  BitExtender #(.inputBits(21), .outputBits(32)) bitextender_2 (
    .in({pulldown_2_out[31], demultiplexer_8_out_1, pulldown_2_out[20], demultiplexer_4_out_1, pulldown_10_out[0]}),
    .out(bitextender_2_out));
  BitExtender #(.inputBits(12), .outputBits(32)) bitextender_3 (.in(demultiplexer_5_out_0), .out(bitextender_3_out));
  Multiplexer #(.Bits(8)) multiplexer_8 (
    .sel(add_1_s[0]), .in_0(pulldown_7_out[7:0]), .in_1(pulldown_7_out[15:8]), .out(pulldown_8_out[7:0]));
  Multiplexer #(.Bits(8)) multiplexer_9 (
    .sel(add_1_s[0]), .in_0(pulldown_7_out[15:8]), .in_1(pulldown_7_out[7:0]), .out(multiplexer_9_out));
  Comparator #(.Bits(4)) comparator_2 (.a(multiplexer_15_out), .b(4'b1101), .eq(comparator_2_eq));  // open: gt, lt
  Comparator #(.Bits(4)) comparator_3 (.a(multiplexer_15_out), .b(4'b0101), .eq(comparator_3_eq));  // open: gt, lt
  Comparator #(.Bits(4)) comparator_4 (.a(multiplexer_15_out), .b(4'b1011), .eq(rom_1_d_2[1]));  // open: gt, lt
  Multiplexer #(.Selector_Bits(2), .Bits(32)) multiplexer_10 (
    .sel(rom_1_d_2), .in_0(bitextender_1_out),
    .in_1({pulldown_2_out[31], demultiplexer_4_out_1, pulldown_2_out[20], demultiplexer_8_out_1, pulldown_2_out[11:0]}),
    .in_2(bitextender_2_out), .in_3(pulldown_3_out), .out(multiplexer_10_out));
  PullDown #(.Bits(32)) pulldown_3 (.out(pulldown_3_out));
  PullDown pulldown_4 (.out(rom_1_d[29]));
  BitExtender #(.inputBits(16), .outputBits(32)) bitextender_4 (.in(pulldown_7_out[15:0]), .out(bitextender_4_out));
  BitExtender #(.outputBits(32)) bitextender_5 (.in(pulldown_8_out[7:0]), .out(bitextender_5_out));
  Multiplexer #(.Bits(32)) multiplexer_11 (
    .sel(demultiplexer_7_out_1), .in_0(d_ff_2_q), .in_1(multiplexer_14_out), .out(multiplexer_11_out));
  assign ImmBus = rom_1_d[17] ? or_4_out : 32'bz;  // Driver driver_1
  PullDown pulldown_5 (.out(pulldown_5_out[1]));
  PullDown pulldown_6 (.out(pulldown_5_out[0]));
  PullDown #(.Bits(16)) pulldown_7 (.out(pulldown_7_out[31:16]));
  PullDown #(.Bits(24)) pulldown_8 (.out(pulldown_8_out[31:8]));
  D_FF #(.Bits(32)) d_ff_2 (.D(multiplexer_11_out), .C(not_1_out), .Q(d_ff_2_q));  // open: nQ
  Multiplexer #(.Bits(32)) multiplexer_12 (
    .sel(IRSwitcher_out), .in_0(d_ff_2_q), .in_1(d_ff_1_q), .out(multiplexer_12_out));
  PullDown pulldown_9 (.out(pulldown_9_out[0]));
  PullDown pulldown_10 (.out(pulldown_10_out[0]));
  BitExtender #(.inputBits(13), .outputBits(32)) bitextender_6 (.in(multiplexer_16_out), .out(bitextender_6_out));
  assign or_4_out = bitextender_6_out | multiplexer_10_out | bitextender_3_out;  // Or or_4, 32 bits wide
  PullDown pulldown_11 (.out(rom_1_d[25]));
  PullDown pulldown_12 (.out(rom_1_d[26]));
  Multiplexer #(.Selector_Bits(2), .Bits(32)) multiplexer_13 (
    .sel(pulldown_5_out), .in_0(pulldown_7_out), .in_1(bitextender_4_out), .in_2(pulldown_8_out),
    .in_3(bitextender_5_out), .out(multiplexer_13_out));
  Multiplexer #(.Bits(32)) multiplexer_14 (
    .sel(rom_1_d[18]), .in_0(MemoryOUTBus), .in_1(32'h13), .out(multiplexer_14_out));
  Multiplexer #(.Bits(32)) multiplexer_15 (
    .sel(d_ff_3_q), .in_0(multiplexer_12_out), .in_1(32'h13),
    .out({multiplexer_15_out_2[31:25], multiplexer_15_out_6, multiplexer_15_out_5, multiplexer_15_out_4, multiplexer_15_out_3, multiplexer_15_out_2[6], multiplexer_15_out, out_5}));
  Demultiplexer #(.Bits(5)) demultiplexer_9 (
    .sel(comparator_5_eq), .in(multiplexer_15_out_3), .out_0({out_11, demultiplexer_9_out_0}),
    .out_1(demultiplexer_9_out_1));
  Multiplexer #(.Bits(13)) multiplexer_16 (
    .sel(and_1_out), .in_0({{2{pulldown_9_out[12]}}, pulldown_9_out[10:5], demultiplexer_9_out_1}),
    .in_1({pulldown_9_out[12], demultiplexer_9_out_1[0], pulldown_9_out[10:5], demultiplexer_9_out_1[4:1], pulldown_9_out[0]}),
    .out(multiplexer_16_out));
  ROM #(.AddrBits(9), .Bits(32)) rom_1 (
    .A({demultiplexer_8_out_0, comparator_6_eq[5], multiplexer_15_out_2[6], multiplexer_15_out}), .sel(1'b1),
    .D({rom_1_d[31:29], pulldown_5_out[0], pulldown_5_out[1], rom_1_d[26:22], rom_1_d_2[0], rom_1_d[20:0]}));
  PullDown pulldown_13 (.out(rom_1_d[23]));
  PullDown pulldown_14 (.out(rom_1_d[24]));
  Multiplexer #(.Bits(32)) multiplexer_17 (
    .sel(rom_1_d[29]), .in_0({ramdualport_1_d, ramdualport_1_d_2}), .in_1(multiplexer_13_out),
    .out(multiplexer_17_out));
  Comparator #(.Bits(4)) comparator_5 (.a(multiplexer_15_out), .b(4'b1000), .eq(comparator_5_eq));  // open: gt, lt
  PullDown pulldown_15 (.out(rom_1_d_2[0]));
  PullDown pulldown_16 (.out(rom_1_d[22]));
  assign MemoryOUTBus = rom_1_d[19] ? multiplexer_17_out : 32'bz;  // Driver driver_2
  not not_1 (not_1_out, CLK);
  and and_1 (and_1_out, comparator_5_eq, multiplexer_15_out_2[6]);
  Multiplexer #(.Bits(7)) multiplexer_18 (
    .sel(or_1_out), .in_0(ImmBus[11:5]), .in_1(pulldown_17_out), .out(multiplexer_18_out));
  PullDown #(.Bits(7)) pulldown_17 (.out(pulldown_17_out));
  assign or_5_out = multiplexer_18_out | demultiplexer_3_out_0;  // Or or_5, 7 bits wide
  Comparator #(.Bits(7)) comparator_6 (.a(or_5_out), .b(7'b0100000), .eq(comparator_6_eq[5]));  // open: gt, lt
  assign RegBus = rom_1_d[23] ? MemoryOUTBus : 32'bz;  // Driver driver_3
  assign RegBus = rom_1_d[22] ? ImmBus : 32'bz;  // Driver driver_4
  PullDown pulldown_18 (.out(rom_1_d[19]));
  PullDown pulldown_19 (.out(rom_1_d[20]));
  PullDown pulldown_20 (.out(rom_1_d[17]));
  PullDown pulldown_21 (.out(rom_1_d[18]));
  PullDown pulldown_22 (.out(rom_1_d[15]));
  PullDown pulldown_23 (.out(rom_1_d[16]));
  PullDown pulldown_24 (.out(rom_1_d[13]));
  PullDown pulldown_25 (.out(rom_1_d[14]));
  PullDown pulldown_26 (.out(rom_1_d[11]));
  PullDown pulldown_27 (.out(rom_1_d[12]));
  Multiplexer #(.Bits(32)) multiplexer_19 (.sel(rom_1_d[14]), .in_0(ImmBus), .in_1(RS2), .out(multiplexer_19_out));
  assign RegBus = rom_1_d[24] ? RS2 : 32'bz;  // Driver driver_5
  PullDown pulldown_28 (.out(rom_1_d[10]));
  PullDown pulldown_29 (.out(rom_1_d[9]));
  D_FF d_ff_3 (.D(HLT), .C(not_2_out), .Q(d_ff_3_q));  // open: nQ
  not not_2 (not_2_out, CLK);
  Sub #(.Bits(32)) sub_1 (.a(MemoryOUTBus), .b(32'h1), .c_i(pulldown_30_out), .s(sub_1_s));  // open: c_o
  PullDown pulldown_30 (.out(pulldown_30_out));
  Decoder #(.Selector_Bits(4)) decoder_1 (
    .sel(demultiplexer_9_out_0), .out_1(decoder_1_out_1), .out_2(decoder_1_out_2), .out_3(decoder_1_out_3),
    .out_4(decoder_1_out_4), .out_5(decoder_1_out_5), .out_6(decoder_1_out_6), .out_7(decoder_1_out_7),
    .out_8(decoder_1_out_8), .out_9(decoder_1_out_9), .out_10(decoder_1_out_10), .out_11(decoder_1_out_11),
    .out_12(decoder_1_out_12), .out_13(decoder_1_out_13), .out_14(decoder_1_out_14), .out_15(decoder_1_out_15));  // open: out_0
  Add #(.Bits(2)) add_1 (
    .a(RS1[1:0]), .b(multiplexer_19_out[1:0]), .c_i(pulldown_31_out), .s(add_1_s), .c_o(add_1_c_o));
  PullDown pulldown_31 (.out(pulldown_31_out));
  PullDown pulldown_32 (.out(rom_1_d[8]));
  PullDown pulldown_33 (.out(rom_1_d[7]));
  and and_2 (and_2_out, RegBus[0], rom_1_d[16]);
  PullDown #(.Bits(2)) pulldown_34 (.out(pulldown_34_out));
  PullDown pulldown_35 (.out(rom_1_d[5]));
  PullDown pulldown_36 (.out(rom_1_d[6]));
  Multiplexer #(.Bits(32)) multiplexer_20 (
    .sel(not_3_out), .in_0(sub_1_s), .in_1(counterpreset_1_out), .out(multiplexer_20_out));
  or or_6 (or_6_out, not_3_out, rom_1_d[1]);
  not not_3 (not_3_out, rom_1_d[0]);
  Multiplexer #(.Selector_Bits(2), .Bits(32)) multiplexer_21 (
    .sel({rom_1_d[3], rom_1_d[4]}), .in_0(RS1), .in_1(MemoryAddressBus), .in_2({pulldown_34_out, RS1[31:2]}),
    .in_3(pulldown_37_out), .out(multiplexer_21_out));
  PullDown #(.Bits(32)) pulldown_37 (.out(pulldown_37_out));
  Multiplexer #(.Bits(32)) multiplexer_22 (
    .sel(rom_1_d[5]), .in_0(multiplexer_19_out),
    .in_1({{3{multiplexer_19_out[31]}}, multiplexer_19_out[30:2]}), .out(multiplexer_22_out));
  and and_3 (and_3_out, rom_1_d[3], rom_1_d[5], add_1_c_o);
  PullDown pulldown_38 (.out(rom_1_d[4]));
  PullDown pulldown_39 (.out(rom_1_d[3]));
  Multiplexer #(.Bits(32)) multiplexer_23 (
    .sel(and_2_out), .in_0(pulldown_40_out), .in_1({{3{ImmBus[31]}}, ImmBus[30:2]}), .out(multiplexer_23_out));
  PullDown #(.Bits(32)) pulldown_40 (.out(pulldown_40_out));
  CounterPreset #(.Bits(32), .isProgramCounter("true")) counterpreset_1 (
    .en(pullup_3_out), .C(CLK), .dir(pulldown_41_out), .in(multiplexer_20_out), .ld(or_6_out),
    .clr(d_ff_3_q), .out(counterpreset_1_out));  // open: ovf
  PullUp pullup_3 (.out(pullup_3_out));
  PullDown pulldown_41 (.out(pulldown_41_out));
  PullDown pulldown_42 (.out(pulldown_42_out));
  PullDown pulldown_43 (.out(rom_1_d[2]));
  PullDown pulldown_44 (.out(rom_1_d[1]));
  Add #(.Bits(32)) add_2 (.a(MemoryAddressBus), .b(multiplexer_23_out), .c_i(not_4_out), .s(add_2_s));  // open: c_o
  not not_4 (not_4_out, and_2_out);
  Add #(.Bits(32)) add_3 (.a(multiplexer_21_out), .b(multiplexer_22_out), .c_i(and_3_out), .s(add_3_s));  // open: c_o
  assign and_4_out = multiplexer_21_out & multiplexer_22_out;  // And and_4, 32 bits wide
  assign xor_1_out = multiplexer_21_out ^ multiplexer_22_out;  // XOr xor_1, 32 bits wide
  BarrelShifter #(.Bits(32)) barrelshifter_1 (
    .in(multiplexer_21_out), .shift(multiplexer_22_out[5:0]), .out(barrelshifter_1_out));
  BarrelShifter #(.Bits(32), .direction("right")) barrelshifter_2 (
    .in(multiplexer_21_out), .shift(multiplexer_22_out[5:0]), .out(barrelshifter_2_out));
  BarrelShifter #(.Bits(32), .barrelShifterMode("arithmetic"), .barrelSigned("true"), .direction("right")) barrelshifter_3 (
    .in(multiplexer_21_out), .shift(multiplexer_22_out[6:0]), .out(barrelshifter_3_out));
  Sub #(.Bits(32)) sub_2 (
    .a(multiplexer_21_out), .b(multiplexer_22_out), .c_i(pulldown_42_out), .s(sub_2_s), .c_o(sub_2_c_o[0]));
  assign or_7_out = multiplexer_21_out | multiplexer_22_out;  // Or or_7, 32 bits wide
  PullDown pulldown_45 (.out(rom_1_d[0]));
  Demultiplexer #(.Bits(32)) demultiplexer_10 (
    .sel(rom_1_d[16]), .in(add_2_s), .out_0(demultiplexer_10_out_0), .out_1(demultiplexer_10_out_1));
  assign MemoryAddressBus = rom_1_d[2] ? counterpreset_1_out : 32'bz;  // Driver driver_6
  Multiplexer #(.Bits(32)) multiplexer_24 (
    .sel(decoder_1_out_1), .in_0(d_ff_4_q), .in_1(RegBus), .out(multiplexer_24_out));
  D_FF #(.Bits(32)) d_ff_4 (.D(multiplexer_24_out), .C(CLK), .Q(d_ff_4_q));  // open: nQ
  Multiplexer #(.Bits(32)) multiplexer_25 (
    .sel(decoder_1_out_2), .in_0(d_ff_5_q), .in_1(RegBus), .out(multiplexer_25_out));
  D_FF #(.Bits(32)) d_ff_5 (.D(multiplexer_25_out), .C(CLK), .Q(d_ff_5_q));  // open: nQ
  Multiplexer #(.Bits(32)) multiplexer_26 (
    .sel(decoder_1_out_3), .in_0(d_ff_6_q), .in_1(RegBus), .out(multiplexer_26_out));
  D_FF #(.Bits(32)) d_ff_6 (.D(multiplexer_26_out), .C(CLK), .Q(d_ff_6_q));  // open: nQ
  Multiplexer #(.Bits(32)) multiplexer_27 (
    .sel(decoder_1_out_4), .in_0(d_ff_7_q), .in_1(RegBus), .out(multiplexer_27_out));
  D_FF #(.Bits(32)) d_ff_7 (.D(multiplexer_27_out), .C(CLK), .Q(d_ff_7_q));  // open: nQ
  Multiplexer #(.Bits(32)) multiplexer_28 (
    .sel(decoder_1_out_5), .in_0(d_ff_8_q), .in_1(RegBus), .out(multiplexer_28_out));
  D_FF #(.Bits(32)) d_ff_8 (.D(multiplexer_28_out), .C(CLK), .Q(d_ff_8_q));  // open: nQ
  Multiplexer #(.Bits(32)) multiplexer_29 (
    .sel(decoder_1_out_6), .in_0(d_ff_9_q), .in_1(RegBus), .out(multiplexer_29_out));
  D_FF #(.Bits(32)) d_ff_9 (.D(multiplexer_29_out), .C(CLK), .Q(d_ff_9_q));  // open: nQ
  Multiplexer #(.Bits(32)) multiplexer_30 (
    .sel(decoder_1_out_7), .in_0(d_ff_10_q), .in_1(RegBus), .out(multiplexer_30_out));
  D_FF #(.Bits(32)) d_ff_10 (.D(multiplexer_30_out), .C(CLK), .Q(d_ff_10_q));  // open: nQ
  Multiplexer #(.Bits(32)) multiplexer_31 (
    .sel(decoder_1_out_8), .in_0(d_ff_11_q), .in_1(RegBus), .out(multiplexer_31_out));
  D_FF #(.Bits(32)) d_ff_11 (.D(multiplexer_31_out), .C(CLK), .Q(d_ff_11_q));  // open: nQ
  Multiplexer #(.Bits(32)) multiplexer_32 (
    .sel(decoder_1_out_9), .in_0(d_ff_12_q), .in_1(RegBus), .out(multiplexer_32_out));
  D_FF #(.Bits(32)) d_ff_12 (.D(multiplexer_32_out), .C(CLK), .Q(d_ff_12_q));  // open: nQ
  Multiplexer #(.Bits(32)) multiplexer_33 (
    .sel(decoder_1_out_10), .in_0(d_ff_13_q), .in_1(RegBus), .out(multiplexer_33_out));
  D_FF #(.Bits(32)) d_ff_13 (.D(multiplexer_33_out), .C(CLK), .Q(d_ff_13_q));  // open: nQ
  Multiplexer #(.Bits(32)) multiplexer_34 (
    .sel(decoder_1_out_11), .in_0(d_ff_14_q), .in_1(RegBus), .out(multiplexer_34_out));
  D_FF #(.Bits(32)) d_ff_14 (.D(multiplexer_34_out), .C(CLK), .Q(d_ff_14_q));  // open: nQ
  Multiplexer #(.Bits(32)) multiplexer_35 (
    .sel(decoder_1_out_12), .in_0(d_ff_15_q), .in_1(RegBus), .out(multiplexer_35_out));
  D_FF #(.Bits(32)) d_ff_15 (.D(multiplexer_35_out), .C(CLK), .Q(d_ff_15_q));  // open: nQ
  Multiplexer #(.Bits(32)) multiplexer_36 (
    .sel(decoder_1_out_13), .in_0(d_ff_16_q), .in_1(RegBus), .out(multiplexer_36_out));
  D_FF #(.Bits(32)) d_ff_16 (.D(multiplexer_36_out), .C(CLK), .Q(d_ff_16_q));  // open: nQ
  Multiplexer #(.Bits(32)) multiplexer_37 (
    .sel(decoder_1_out_14), .in_0(d_ff_17_q), .in_1(RegBus), .out(multiplexer_37_out));
  D_FF #(.Bits(32)) d_ff_17 (.D(multiplexer_37_out), .C(CLK), .Q(d_ff_17_q));  // open: nQ
  Multiplexer #(.Bits(32)) multiplexer_38 (
    .sel(decoder_1_out_15), .in_0(d_ff_18_q), .in_1(RegBus), .out(multiplexer_38_out));
  D_FF #(.Bits(32)) d_ff_18 (.D(multiplexer_38_out), .C(CLK), .Q(d_ff_18_q));  // open: nQ
  PullDown #(.Bits(32)) pulldown_46 (.out(pulldown_46_out));
  assign RegBus = demultiplexer_11_out_0 ? {demultiplexer_10_out_0[29:0], pulldown_47_out} : 32'bz;  // Driver driver_7
  PullDown #(.Bits(2)) pulldown_47 (.out(pulldown_47_out));
  assign RS1 = decoder_2_out_0 ? pulldown_46_out : 32'bz;  // Driver driver_8
  assign RS2 = decoder_3_out_0 ? pulldown_46_out : 32'bz;  // Driver driver_9
  assign RS1 = decoder_2_out_1 ? d_ff_4_q : 32'bz;  // Driver driver_10
  assign RS2 = decoder_3_out_1 ? d_ff_4_q : 32'bz;  // Driver driver_11
  assign RS1 = decoder_2_out_2 ? d_ff_5_q : 32'bz;  // Driver driver_12
  assign RS2 = decoder_3_out_2 ? d_ff_5_q : 32'bz;  // Driver driver_13
  assign RS1 = decoder_2_out_3 ? d_ff_6_q : 32'bz;  // Driver driver_14
  assign RS2 = decoder_3_out_3 ? d_ff_6_q : 32'bz;  // Driver driver_15
  assign RS1 = decoder_2_out_4 ? d_ff_7_q : 32'bz;  // Driver driver_16
  assign RS2 = decoder_3_out_4 ? d_ff_7_q : 32'bz;  // Driver driver_17
  assign RS1 = decoder_2_out_5 ? d_ff_8_q : 32'bz;  // Driver driver_18
  assign RS2 = decoder_3_out_5 ? d_ff_8_q : 32'bz;  // Driver driver_19
  assign RS1 = decoder_2_out_6 ? d_ff_9_q : 32'bz;  // Driver driver_20
  assign RS2 = decoder_3_out_6 ? d_ff_9_q : 32'bz;  // Driver driver_21
  assign RS1 = decoder_2_out_7 ? d_ff_10_q : 32'bz;  // Driver driver_22
  assign RS2 = decoder_3_out_7 ? d_ff_10_q : 32'bz;  // Driver driver_23
  assign RS1 = decoder_2_out_8 ? d_ff_11_q : 32'bz;  // Driver driver_24
  assign RS2 = decoder_3_out_8 ? d_ff_11_q : 32'bz;  // Driver driver_25
  assign RS1 = decoder_2_out_9 ? d_ff_12_q : 32'bz;  // Driver driver_26
  assign RS2 = decoder_3_out_9 ? d_ff_12_q : 32'bz;  // Driver driver_27
  assign RS1 = decoder_2_out_10 ? d_ff_13_q : 32'bz;  // Driver driver_28
  assign RS2 = decoder_3_out_10 ? d_ff_13_q : 32'bz;  // Driver driver_29
  assign RS1 = decoder_2_out_11 ? d_ff_14_q : 32'bz;  // Driver driver_30
  assign RS2 = decoder_3_out_11 ? d_ff_14_q : 32'bz;  // Driver driver_31
  assign RS1 = decoder_2_out_12 ? d_ff_15_q : 32'bz;  // Driver driver_32
  assign RS2 = decoder_3_out_12 ? d_ff_15_q : 32'bz;  // Driver driver_33
  assign RS1 = decoder_2_out_13 ? d_ff_16_q : 32'bz;  // Driver driver_34
  assign RS2 = decoder_3_out_13 ? d_ff_16_q : 32'bz;  // Driver driver_35
  assign RS1 = decoder_2_out_14 ? d_ff_17_q : 32'bz;  // Driver driver_36
  assign RS2 = decoder_3_out_14 ? d_ff_17_q : 32'bz;  // Driver driver_37
  assign RS1 = decoder_2_out_15 ? d_ff_18_q : 32'bz;  // Driver driver_38
  assign RS2 = decoder_3_out_15 ? d_ff_18_q : 32'bz;  // Driver driver_39
  Multiplexer #(.Selector_Bits(3), .Bits(32)) multiplexer_39 (
    .sel({rom_1_d[6], rom_1_d[7], rom_1_d[8]}), .in_0(add_3_s), .in_1(and_4_out), .in_2(xor_1_out),
    .in_3(barrelshifter_1_out), .in_4(barrelshifter_2_out), .in_5(barrelshifter_3_out), .in_6(sub_2_s),
    .in_7(or_7_out), .out(multiplexer_39_out));
  assign MemoryOUTBus = demultiplexer_11_out_1 ? demultiplexer_10_out_1 : 32'bz;  // Driver driver_40
  PullDown #(.Bits(31)) pulldown_48 (.out(pulldown_48_out));
  Demultiplexer demultiplexer_11 (
    .sel(rom_1_d[16]), .in(rom_1_d[12]), .out_0(demultiplexer_11_out_0), .out_1(demultiplexer_11_out_1));
  PullDown #(.Bits(31)) pulldown_49 (.out(pulldown_49_out));
  not not_5 (not_5_out[0], multiplexer_39_out[31]);
  PullDown #(.Bits(31)) pulldown_50 (.out(pulldown_50_out));
  not not_6 (not_6_out[0], sub_2_c_o[0]);
  PullDown #(.Bits(31)) pulldown_51 (.out(pulldown_51_out));
  assign {or_8_out_4, or_8_out_3, or_8_out_2, or_8_out} = multiplexer_39_out[7:0] | multiplexer_39_out[15:8] | multiplexer_39_out[23:16] | multiplexer_39_out[31:24];  // Or or_8, 8 bits wide
  PullDown #(.Bits(2)) pulldown_52 (.out(pulldown_52_out));
  not not_7 (not_7_out[0], or_9_out[0]);
  PullDown #(.Bits(31)) pulldown_53 (.out(pulldown_53_out));
  PullDown #(.Bits(31)) pulldown_54 (.out(pulldown_54_out));
  or or_9 (or_9_out[0], or_10_out[0], or_10_out[1]);
  Multiplexer #(.Selector_Bits(3), .Bits(32)) multiplexer_40 (
    .sel({rom_1_d[9], rom_1_d[10], rom_1_d[11]}), .in_0(multiplexer_39_out),
    .in_1({pulldown_49_out, multiplexer_39_out[31]}), .in_2({pulldown_48_out, sub_2_c_o[0]}),
    .in_3({multiplexer_39_out[29:0], pulldown_52_out}), .in_4({pulldown_50_out, not_5_out[0]}),
    .in_5({pulldown_51_out, not_6_out[0]}), .in_6({pulldown_53_out, not_7_out[0]}),
    .in_7({pulldown_54_out, or_9_out[0]}), .out(multiplexer_40_out));
  assign or_10_out = or_8_out | or_8_out_2 | or_8_out_3 | or_8_out_4;  // Or or_10, 2 bits wide
  Decoder #(.Selector_Bits(4)) decoder_2 (
    .sel(demultiplexer_6_out_0[3:0]), .out_0(decoder_2_out_0), .out_1(decoder_2_out_1),
    .out_2(decoder_2_out_2), .out_3(decoder_2_out_3), .out_4(decoder_2_out_4), .out_5(decoder_2_out_5),
    .out_6(decoder_2_out_6), .out_7(decoder_2_out_7), .out_8(decoder_2_out_8), .out_9(decoder_2_out_9),
    .out_10(decoder_2_out_10), .out_11(decoder_2_out_11), .out_12(decoder_2_out_12),
    .out_13(decoder_2_out_13), .out_14(decoder_2_out_14), .out_15(decoder_2_out_15));
  Decoder #(.Selector_Bits(4)) decoder_3 (
    .sel(demultiplexer_5_out_1[3:0]), .out_0(decoder_3_out_0), .out_1(decoder_3_out_1),
    .out_2(decoder_3_out_2), .out_3(decoder_3_out_3), .out_4(decoder_3_out_4), .out_5(decoder_3_out_5),
    .out_6(decoder_3_out_6), .out_7(decoder_3_out_7), .out_8(decoder_3_out_8), .out_9(decoder_3_out_9),
    .out_10(decoder_3_out_10), .out_11(decoder_3_out_11), .out_12(decoder_3_out_12),
    .out_13(decoder_3_out_13), .out_14(decoder_3_out_14), .out_15(decoder_3_out_15));
  assign RegBus = decoder_4_out_3 ? multiplexer_40_out : 32'bz;  // Driver driver_41
  assign MemoryOUTBus = decoder_4_out_2 ? multiplexer_40_out : 32'bz;  // Driver driver_42
  assign MemoryAddressBus = decoder_4_out_1 ? multiplexer_40_out : 32'bz;  // Driver driver_43
  Decoder #(.Selector_Bits(2)) decoder_4 (
    .sel({rom_1_d[13], rom_1_d[15]}), .out_0(NOT_EN), .out_1(decoder_4_out_1), .out_2(decoder_4_out_2),
    .out_3(decoder_4_out_3));

  assign out_9 = MemoryAddressBus[31:20];

  // Notes on the sheet:
  //   CLK: Hz: 100
  //   HLT: default 1
  //   INPUT
  //   R type
  //   ~I_type
  //   This is here because 
  //   only the last
  //   field differs in 
  //   R/S/B types.
  //   B1
  //   Byte in
  //   Half in
  //   Word in
  //   Hack to allow overwriting only one
  //   byte/ one half, by forcing ram
  //   to always output, and
  //   using our own tri state to
  //   control output essentially 
  //   bypassing the ram's internal
  //   tri-state.
  //   B2
  //   I type
  //   J type
  //   The other half
  //   The other byte
  //   LOAD_IR
  //   U type
  //   Control Logic
  //   Pipeline / Instruction Register
  //   IR2
  //   U/J type
  //   RD(5)
  //   Select half
  //   Swap bytes within 
  //   halfs to select
  //   the right byte
  //   RS1(5)
  //   RS2(5)
  //   proper B type 
  //   handling
  //   proper J type 
  //   handling
  //   RAM_OUTSWTCH B3
  //   Select byte of 
  //   selected half
  //   IR1
  //   Decoding UNIT
  //   S/B type
  //   IMM(32)
  //   RAM_OUTSWTCH B1
  //   RAM_OUTSWTCH B2
  //   NOTE:
  //   If you don't want the first
  //   instruction to be skipped
  //   you should pulse the clock
  //   once ( technically you only need a
  //   low to high clock edge )
  //    wihile in HLT to fill the IRs (a.k.a pipeline)
  //   Half 0-ext
  //   Half sign-ext
  //   Byte 0-ext
  //   Byte sign-ext
  //   ID
  //   funct7
  //   funct3
  //   This allows storing memory output
  //   to registers
  //   This allows storing the immediate
  //   to registers
  //   RAM_INSWTCH B1
  //   RAM_INSWTCH B2
  //   NOOP here can also be used as a way
  //   to defer LOAD-ing to the next 
  //   instruction (a.k.a creating a 
  //   pipeline stall) to the next cycle 
  //   if the current instruction needs 
  //   access to ram in some way which 
  //   can not be done in parallel with LOAD.
  //   Control signals change on the
  //   down-clock, since that's
  //   when we DECODE.
  //   We EXECUTE and FETCH on
  //   the up-clock.
  //   This muxer is here
  //   to stop the cpu from
  //   executing the instruction
  //   that is cached in the IRs
  //   while in RST. To achive that
  //   it replaces all instructions
  //   that sould have otherwise 
  //   gone to the decoder 
  //   with NOOps.
  //   B type
  //   High bit
  //   Low nibble
  //   contents of rom_1 (hex, n*v repeats v):
  //   288e8028,80005,80005,80005,aa005,2aac35,80005,80005,5168028,80005,80005,80005,8e005,
  //   6a0005,80005,80005,80005,80005,80005,80005,80005,80005,80005,80005,7f687,6302f,80005,
  //   63037,80005,80005,80005,80005,288e8028,80005,80005,80005,aa005,2aac35,80005,80005,
  //   5168028,80005,80005,80005,8e0c5,6a0005,80005,80005,80005,80005,80005,80005,80005,
  //   80005,80005,80005,7f687,6302f,80005,63037,80005,80005,80005,80005,208e8028,80005,
  //   80005,80005,aa185,2aac35,80005,80005,7168028,80005,80005,80005,8e185,6a0005,80005,
  //   80005,80005,80005,80005,80005,80005,80005,80005,80005,7fe87,6302f,80005,63037,80005,
  //   80005,80005,80005,208e8028,80005,80005,80005,aa185,2aac35,80005,80005,7168028,80005,
  //   80005,80005,8e185,6a0005,80005,80005,80005,80005,80005,80005,80005,80005,80005,80005,
  //   7fe87,6302f,80005,63037,80005,80005,80005,80005,8e8028,80005,80005,80005,aa8c5,2aac35,
  //   80005,80005,1168028,80005,80005,80005,8e8c5,6a0005,80005,80005,80005,80005,80005,
  //   80005,80005,80005,80005,80005,80005,6302f,80005,63037,80005,80005,80005,80005,8e8028,
  //   80005,80005,80005,aa8c5,2aac35,80005,80005,1168028,80005,80005,80005,8e8c5,6a0005,
  //   80005,80005,80005,80005,80005,80005,80005,80005,80005,80005,80005,6302f,80005,63037,
  //   80005,80005,80005,80005,80005,80005,80005,80005,aa4c5,2aac35,80005,80005,80005,80005,
  //   80005,80005,8e4c5,6a0005,80005,80005,80005,80005,80005,80005,80005,80005,80005,80005,
  //   80005,6302f,80005,63037,80005,80005,80005,80005,80005,80005,80005,80005,aa4c5,2aac35,
  //   80005,80005,80005,80005,80005,80005,8e4c5,6a0005,80005,80005,80005,80005,80005,80005,
  //   80005,80005,80005,80005,80005,6302f,80005,63037,80005,80005,80005,80005,388e8028,
  //   80005,80005,80005,aa085,2aac35,80005,80005,80005,80005,80005,80005,8e085,6a0005,80005,
  //   80005,80005,80005,80005,80005,80005,80005,80005,80005,7f8c7,6302f,80005,63037,80005,
  //   80005,80005,80005,388e8028,80005,80005,80005,aa085,2aac35,80005,80005,80005,80005,
  //   80005,80005,8e085,6a0005,80005,80005,80005,80005,80005,80005,80005,80005,80005,80005,
  //   7f8c7,6302f,80005,63037,80005,80005,80005,80005,308e8028,80005,80005,80005,aa045,
  //   2aac35,80005,80005,80005,80005,80005,80005,8e045,6a0005,80005,80005,80005,80005,80005,
  //   80005,80005,80005,80005,80005,7f2c7,6302f,80005,63037,80005,80005,80005,80005,308e8028,
  //   80005,80005,80005,aa145,2aac35,80005,80005,80005,80005,80005,80005,8e145,6a0005,80005,
  //   80005,80005,80005,80005,80005,80005,80005,80005,80005,7f2c7,6302f,80005,63037,80005,
  //   80005,80005,80005,80005,80005,80005,80005,aa1c5,2aac35,80005,80005,80005,80005,80005,
  //   80005,8e1c5,6a0005,80005,80005,80005,80005,80005,80005,80005,80005,80005,80005,7f4c7,
  //   6302f,80005,63037,80005,80005,80005,80005,80005,80005,80005,80005,aa1c5,2aac35,80005,
  //   80005,80005,80005,80005,80005,8e1c5,6a0005,80005,80005,80005,80005,80005,80005,80005,
  //   80005,80005,80005,7f4c7,6302f,80005,63037,80005,80005,80005,80005,80005,80005,80005,
  //   80005,aa105,2aac35,80005,80005,80005,80005,80005,80005,8e105,6a0005,80005,80005,80005,
  //   80005,80005,80005,80005,80005,80005,80005,7fac7,6302f,80005,63037,80005,80005,80005,
  //   80005,80005,80005,80005,80005,aa105,2aac35,80005,80005,80005,80005,80005,80005,8e105,
  //   6a0005,80005,80005,80005,80005,80005,80005,80005,80005,80005,80005,7fac7,6302f,80005,
  //   63037,80005,80005,80005,80005
  //   Control Lines
  //   MOUTB TO RINB
  //   REG_OUT
  //   B3
  //   CNTRL_UPIMM
  //   ROUTB TO RINB
  //   Hack for
  //   I immediate
  //   in SRAI/SRLI
  //   RAM_ENO
  //   RAM_LOAD
  //   CNTRL_IMM_OUT
  //   IR_NOP
  //   ALU__OUT B0
  //   AAU_SWTCHMOD
  //   ALU_SWTCHB_REG
  //   ALU_OUT B1
  //   ALU_OUTMOD B0
  //   AAU_OUT
  //   Hardcoded arithmetic 
  //   shift right by 2.
  //   Translates byte offset to
  //   native offset.
  //   This gives us the amount we need to branch.
  //   Hardcoded logical 
  //   shift right by 2.
  //   Translates byte address to
  //   native address.
  //   ALU_OUTMOD B1
  //   ALU_OUTMOD B2
  //   Hack for 
  //   jumps/branches,
  //   for pipeline
  //   stall (nop)
  //   Hardcoded arithmetic 
  //   shift right by 2.
  //   Translates byte offset to
  //   native offset.
  //   ALU_OP B0
  //   ALU_OP B1
  //   Branch switcher.
  //   Detects if we need to jump or not,
  //    if not it makes the AAU ignore
  //   the addition and instead just add 1.
  //   If we are using 
  //   load/store instructions 
  //   then this will be the last 
  //   2 bits of the byte-result.
  //   ALU_TRANSB
  //   ALU_OP B2
  //   HLT can only be changed
  //   on the down-clock so the
  //   instruction which is cached in the
  //   irs ( a.k.a the first instruction )
  //   gets to be parsed instead of
  //   acting like a no-op.
  //   If HLT were to change
  //   on a high clock
  //   then there would have
  //   never been a down clock before
  //   it, which means the cpu
  //   didn't load the instruction
  //   even though it thinks so
  //   which causes it to skip
  //   over it.
  //   Address Arithmetic UNIT
  //   Enables input, but also enables counting,
  //   but if load is on it will latch the value
  //   instead of counting
  //   ALU_SWTCHA B0
  //   ALU_SWTCHA B1
  //   N.B.
  //   If the last bit is on 
  //   we should branch.
  //   RS1
  //   IMM/RS2
  //   PC_OUT
  //   PC_LOAD
  //   PC
  //   Register File
  //   PC_ENIN/_ENC
  //   Note
  //   We store byte addresses in registers
  //   to make the effect of programs is consistent with the spec
  //   even though internally we use native addresses.
  //   Logical shift left
  //   (Translates native address 
  //   to byte address for
  //   storage in regs)
  //   No need to Logical shift left, 
  //   when in branch mode, because the
  //   address is already native.
  //   If not in branch mode then always add 1 to input ( input is native ).
  //   Othwerwise if in branch mode then if we should jump output the pc+offset, then the pc will sub 1 and allow the 
  //   branch delay slot nop to work.
  //   If we shouldn't jump then just output the address of the next instruction (a.k.a addres+1) since we basically just 
  //   want to jump to the next instruction.
  //   Arithmetic and Logic UNIT
  //   Branch mode
  //   CLK
  //   SUBC
  //   SIGNBIT
  //   Enable out
  //   Hardcoded
  //   shift left by 2.
  //   Translate native address
  //   to byte oriented address
  //   .
  //   Note: yes, there is a difference
  //   between testing wheter the 
  //   result is negative (a.k.a sign bit is 1)
  //   and looking at wheter the
  //   carry out of subtraction is set.
  //   that differance occurs, 
  //   when dealing with unsigned 
  //   numbers  that use the first bit,
  //   because 0xFFFFFFFF. is negative in 
  //   32-bit 2's complement but positive 
  //   if treated as unsigned so 
  //   basically the carry out of
  //   subtraction is a little like
  //   the sign bit of a 33-bit
  //   adder where the second
  //   input is inverted and Cin is on,
  //   i think.
  //   This differnce was encountered when
  //   implementing SLTI and SLTIU.
  //   SEL1
  //   SEL2
endmodule
